# Fritzing sketch sketch (saved by Fritzing 0.9.3b)
breadboards: 1

parts:
  R1 = Resistor [tolerance=±5% resistance=220 package=THT]
  R2 = Resistor [tolerance=±5% resistance=220 package=THT]
  R3 = Resistor [tolerance=±5% resistance=220 package=THT]
  R4 = Resistor [tolerance=±5% resistance=220 package=THT]
  R5 = Resistor [tolerance=±5% resistance=220 package=THT]
  LED6 = smd LED [color="Red (633nm)" package="0805 [SMD]"]
  LED7 = smd LED [color="Yellow (592nm)" package="0805 [SMD]"]
  LED8 = smd LED [color="Blue (430nm)" package="0805 [SMD]"]
  LED9 = smd LED [color="White (4500K)" package="0805 [SMD]"]
  LED10 = smd LED [color="Green (560nm)" package="0805 [SMD]"]
  Componente2 = Arduino Ethernet Shield (Rev3)
  T1 = TMP36 Temperature Sensor [package="TO92 [THT]"]

nets:
  GND: R1.Pin_0, R2.Pin_0, R3.Pin_0, R4.Pin_0, R5.Pin_0, Componente2.GND, T1.GND
  N1: R1.Pin_1, LED10.anode
  N2: R2.Pin_1, LED9.anode
  N3: R3.Pin_1, LED8.anode
  N4: R4.Pin_1, LED6.anode
  N5: R5.Pin_1, LED7.anode
  N6: Componente2.A0, T1.Vout
  N7: Componente2.5V, T1.+Vs
